# Fritzing sketch battery-toolbox (saved by Fritzing 0.9.6b)
breadboards: 1

parts:
  U1 = LCD-16X2 [package=lcd-16x2_noholes]
  R3 = Resistor [tolerance=±5% power=0.25 resistance=220 package=THT]
  R4 = Trimmer Potentiometer [maximum_resistance=25kΩ package=THT]
  U4_(Rotary_encoder) = ENCODER-QUADRATURE [package=encoder-16mm-quad]
  C3 = Ceramic Capacitor [capacitance=100nF voltage=35V package="100 mil [THT, multilayer]"]
  C4 = Ceramic Capacitor [capacitance=100nF voltage=35V package="100 mil [THT, multilayer]"]
  S1_(Rotary_Push)1 = Pushbutton [package="[THT]"]
  C5 = Ceramic Capacitor [capacitance=100nF voltage=35V package="100 mil [THT, multilayer]"]
  R8 = Resistor [tolerance=±5% power=0.25 resistance=50k package=THT]
  R9 = Resistor [tolerance=±5% power=0.25 resistance=22 package=THT]
  D2 = Zener Diode [breakdown_voltage=4.7V part_number=1N4732A package="Melf DO-213 AB [SMD]"]
  Part2 = Arduino Uno (Rev3)
  U5 = ACS712 [package=so08]
  V4 = DC Power [voltage=12V part_number="Car Battery"]
  Q2 = Basic FET N-Channel [part_number=D472 package="D2Pak [SMD]"]
  Q3 = Basic FET N-Channel [part_number=D472 package="D2Pak [SMD]"]
  Fuse1 = Fuse with Handler [part_number=Htc-15A]
  C6 = Ceramic Capacitor [capacitance=1nF voltage=35V package="100 mil [THT, multilayer]"]
  R10 = Resistor [tolerance=±5% power=0.25 resistance=1.8k package=THT]
  R11 = Resistor [tolerance=±5% power=0.25 resistance=47k package=THT]
  C7 = Ceramic Capacitor [capacitance=100nF voltage=35V package="100 mil [THT, multilayer]"]
  C8 = Ceramic Capacitor [capacitance=100nF voltage=35V package="100 mil [THT, multilayer]"]
  L1 = Inductor [part_number="10 μH" package="400 mil [THT]"]
  R12 = Resistor [tolerance=±5% power=0.25 resistance=10k package=THT]
  R13 = Resistor [tolerance=±1% power=0.25W resistance=6190 package=THT]
  R14 = Resistor [tolerance=±1% power=0.25 resistance=20k package=THT]
  R15 = Trimmer Potentiometer [maximum_resistance=5k package=THT]
  C10 = Electrolytic Capacitor [capacitance=1µF voltage=6.3V package="100 mil [THT, electrolytic]"]
  C11 = Electrolytic Capacitor [capacitance=10µF voltage=6.3V package="100 mil [THT, electrolytic]"]
  R16 = Temperature Sensor (Thermistor) [thermistor_type=NTC part_number="B3950 (100K)" package=THT]
  R17 = Resistor [tolerance=±5% power=0.25 resistance=4.7k package=THT]
  R18 = Resistor [tolerance=±5% power=0.25 resistance=10k package=THT]
  L2 = Inductor [part_number="10 μH" package="400 mil [THT]"]
  R19 = Resistor [tolerance=±5% power=0.25 resistance=10k package=THT]
  R20 = Resistor [tolerance=±5% power=0.25 resistance=10k package=THT]
  C12 = Electrolytic Capacitor [capacitance=1µF voltage=6.3V package="100 mil [THT, electrolytic]"]
  R21 = Resistor [tolerance=±5% power=100W resistance=2 package=THT]
  Fuse2 = Fuse with Handler [part_number=Htc-15A]
  C13 = Electrolytic Capacitor [capacitance=1mF voltage=6.3V package="100 mil [THT, electrolytic]"]

nets:
  GND: U1.VSS, U1.R_W, R4.leg2, U4_(Rotary_encoder).C, C3.0, C4.0, S1_(Rotary_Push)1.Pin_3, S1_(Rotary_Push)1.Pin_4, C5.0, D2.anode, Part2.GND, U5.GND, V4.V-, C6.0, R11.Pin_0, C7.0, C8.0, R13.Pin_1, C10.-, C11.-, R17.Pin_0, C12.-, R21.Pin_1, C13.-
  5V: U1.VDD, U1.K, R3.Pin_1, R4.leg1, R8.Pin_1, R9.Pin_1, Part2.5V, U5.VCC, C8.1, C13.+
  N1: U1.VO, R4.wiper
  N2: U1.RS, Part2.D13/SCK
  N3: U1.E, Part2.D12/MISO
  N4: U1.DB4, Part2.D8
  N5: U1.DB5, Part2.D7
  N6: U1.DB6, Part2.D5_PWM
  N7: U1.DB7, Part2.D4
  N8: U1.A, R3.Pin_0
  N9: U4_(Rotary_encoder).A, C3.1, Part2.D2
  N10: U4_(Rotary_encoder).B, C4.1, Part2.D3_PWM
  N11: S1_(Rotary_Push)1.Pin_1, S1_(Rotary_Push)1.Pin_2, C5.1, R8.Pin_0, Part2.A4/SDA
  N12: R9.Pin_0, D2.cathode, Part2.AREF, C11.+, R16.pin_1
  N13: Part2.A0, R14.Pin_1, R15.leg1, R15.wiper
  N14: Part2.A1, R10.Pin_1, R11.Pin_1, C7.1
  N15: Part2.A2, R16.pin_0, R17.Pin_1
  N16: Part2.D9_PWM, R19.Pin_1
  N17: Part2.D10_PWM/SS, R12.Pin_1
  N18: U5.IP+, Q2.source, Q3.drain
  N19: U5.IP-, Fuse1.Connector1, R14.Pin_0
  N20: U5.FILT, C6.1
  N21: U5.VOUT, R10.Pin_0
  N22: V4.V+, Fuse1.Connector2
  N23: Q2.Gate, R18.Pin_0
  N24: Q2.drain, Fuse2.Connector2
  N25: Q3.Gate, R20.Pin_0
  N26: Q3.source, R21.Pin_0
  N27: L1.pin_0, C10.+, R18.Pin_1
  N28: L1.pin_1, R12.Pin_0
  N29: R13.Pin_0, R15.leg2
  N30: L2.pin_0, R20.Pin_1, C12.+
  N31: L2.pin_1, R19.Pin_0
  14V: Fuse2.Connector1
